# Fritzing sketch localPanel (saved by Fritzing 0.9.3b)

parts:
  WeMos_D1_Mini1 = WeMos D1 Mini
  Part1 = Arduino Mega 2560 (Rev3)
  Part2 = LCD Keypad Shield  # not connected

nets:
  N1: WeMos_D1_Mini1.G, Part1.GND
  N2: WeMos_D1_Mini1.RX, Part1.D18/TX1
  N3: WeMos_D1_Mini1.TX, Part1.D19/RX1

notes:
  Local Pane

custom parts:
  LCD Keypad Shield: It consists of a 1602 white character blue backlight LCD. The keypad consists of 5 keys — select, up, right, down and left. To save the digital IO pins, the keypad interface uses only one ADC channel. The key value is read through a 5 stage voltage divider.
